# Fritzing sketch draw (saved by Fritzing 0.9.2b)
breadboards: 1

parts:
  Componente1 = Arduino Uno (Rev3)
  LED1 = LED - 5mm [color="Green (570nm)" package="5 mm [THT]"]
  LED2 = LED - 5mm [color="Red (660nm)" package="5 mm [THT]"]
  LED3 = LED - 5mm [color="Green (570nm)" package="5 mm [THT]"]
  LED4 = LED - 5mm [color="Red (660nm)" package="5 mm [THT]"]
  LED5 = LED - 5mm [color="Green (570nm)" package="5 mm [THT]"]
  LED6 = LED - 5mm [color="Red (660nm)" package="5 mm [THT]"]
  R1 = Resistor [tolerance=±5% resistance=330 package=THT]
  R2 = Resistor [tolerance=±5% resistance=330 package=THT]
  R3 = Resistor [tolerance=±5% resistance=330 package=THT]
  R4 = Resistor [tolerance=±5% resistance=330 package=THT]
  R5 = Resistor [tolerance=±5% resistance=330 package=THT]
  R6 = Resistor [tolerance=±5% resistance=330 package=THT]

nets:
  N1: Componente1.D9_PWM, R4.Pin_0
  N2: Componente1.D10_PWM/SS, R5.Pin_0
  N3: Componente1.D11_PWM/MOSI, R6.Pin_0
  N4: Componente1.D3_PWM, R1.Pin_0
  N5: Componente1.D5_PWM, R2.Pin_0
  N6: Componente1.D6_PWM, R3.Pin_0
  N7: Componente1.GND, LED1.cathode, LED2.cathode, LED3.cathode, LED4.cathode, LED5.cathode, LED6.cathode
  N8: LED1.anode, R6.Pin_1
  N9: LED2.anode, R5.Pin_1
  N10: LED3.anode, R4.Pin_1
  N11: LED4.anode, R3.Pin_1
  N12: LED5.anode, R2.Pin_1
  N13: LED6.anode, R1.Pin_1
